# Fritzing sketch scheme (saved by Fritzing 0.9.3b)
breadboards: 1

parts:
  WeMos_D1_Mini1 = WeMos D1 Mini
  S2 = Momentary Switch [package=ksa_sealed_tac_switch]
  J1 = Screw terminal - 2 pins [package=THT]

nets:
  N1: WeMos_D1_Mini1.D0, WeMos_D1_Mini1.RST
  N2: WeMos_D1_Mini1.G, S2.1, S2.3, J1.pin1
  N3: S2.2, S2.4

notes:
  VarlamovGeorge
  To water meter
